# Fritzing sketch Arduino_EG (saved by Fritzing 0.9.3b)
breadboards: 1

parts:
  パーツ1 = Arduino Pro Mini (5V)  # not connected
  R1 = Rotary Potentiometer (Small) [maximum_resistance=100kΩ package=THT]
  R2 = Rotary Potentiometer (Small) [maximum_resistance=100kΩ package=THT]
  R3 = Rotary Potentiometer (Small) [maximum_resistance=100kΩ package=THT]
  R4 = Rotary Potentiometer (Small) [maximum_resistance=100kΩ package=THT]
  D1 = Rectifier Diode [part_number=1N4001 package="300 mil [THT]"]
  Q1 = Basic FET P-Channel [package="TO220 [THT]"]
  Q2 = PNP-Transistor [package="TO92 [THT]"]
  D2 = Rectifier Diode [part_number=1N4001 package="300 mil [THT]"]
  S1 = Round Pushbutton
  C1 = Electrolytic Capacitor [capacitance=1µF package="100 mil [THT, electrolytic]"]
  R5 = Resistor [tolerance=±5% resistance=1k package=THT]
  LED1 = LED - 5mm [color="Red (633nm)" package="5 mm [THT]"]
  IC1 = Dual Op-Amp [package=dip08]
  C2 = Ceramic Capacitor [capacitance=100nF package="100 mil [THT, multilayer]"]

nets:
  N1: R1.leg1, R2.leg1, R4.leg1, C1.+, IC1.B_+IN
  N2: R1.wiper, D1.cathode
  N3: R2.wiper, Q2.E
  N4: R3.leg1, Q1.drain
  N5: R3.wiper, Q2.C
  N6: R3.leg2, IC1.A_V+, C2.0
  N7: R4.wiper, D2.cathode
  N8: Q1.gate, Q2.B, S1.leg1, C1.-, LED1.cathode, IC1.A_+IN, IC1.A_V-, C2.1
  N9: R5.Pin_0, LED1.anode
  N10: IC1.A_OUT, IC1.A_-IN
  N11: IC1.B_-IN, IC1.B_OUT

notes:
  Attack
  Decay
  Sustain
  Release
  OUT
  2N7000
  S / D / G
  2SA1015
  E / C / B
  GND
  +5V
  GateIn
