# Fritzing sketch Arduino_EG_Attack_Charge_Test (saved by Fritzing 0.9.3b)
breadboards: 1

parts:
  パーツ1 = Arduino Uno (Rev3)
  R1 = Rotary Potentiometer (Small) [maximum_resistance=100kΩ package=THT]
  D1 = Rectifier Diode [part_number=1N4001 package="300 mil [THT]"]
  C1 = Electrolytic Capacitor [capacitance=1µF package="100 mil [THT, electrolytic]"]
  S2 = Round Pushbutton
  R2 = Resistor [tolerance=±5% resistance=100 package=THT]

nets:
  N1: パーツ1.A0, R1.leg1, C1.+, R2.Pin_1
  N2: パーツ1.D2, S2.leg0
  N3: パーツ1.D4, D1.anode
  N4: パーツ1.D5_PWM, R2.Pin_0
  N5: パーツ1.GND, C1.-, S2.leg1
  N6: R1.wiper, D1.cathode

notes:
  10k/A
  Check
  Pin
  OUT
