# Fritzing sketch Arduino_EG_Impl_Test (saved by Fritzing 0.9.3b)
breadboards: 1

parts:
  パーツ1 = Arduino Pro Mini (5V)  # not connected
  R1 = Resistor [tolerance=±5% resistance=10k package=THT]
  C1 = Electrolytic Capacitor [capacitance=1µF package="100 mil [THT, electrolytic]"]
  R2 = Rotary Potentiometer (Small) [maximum_resistance=100kΩ package=THT]
  D1 = Rectifier Diode [part_number=1N4001 package="300 mil [THT]"]
  R3 = Rotary Potentiometer (Small) [maximum_resistance=100kΩ package=THT]
  Q1 = Basic FET P-Channel [package="TO220 [THT]"]
  R4 = Resistor [tolerance=±5% resistance=1M package=THT]
  R5 = Rotary Potentiometer (Small) [maximum_resistance=100kΩ package=THT]
  Q2 = PNP-Transistor [package="TO92 [THT]"]
  R6 = Resistor [tolerance=±5% resistance=6.8k package=THT]
  R7 = Rotary Potentiometer (Small) [maximum_resistance=100kΩ package=THT]
  D2 = Rectifier Diode [part_number=1N4001 package="300 mil [THT]"]
  R8 = Rotary Potentiometer (Small) [maximum_resistance=100kΩ package=THT]
  IC1 = Dual Op-Amp [package=dip08]
  C2 = Ceramic Capacitor [capacitance=100nF package="100 mil [THT, multilayer]"]
  R9 = Resistor [tolerance=±5% resistance=1k package=THT]
  LED1 = LED - 3mm [color="Red (633nm)" package="3 mm [THT]"]
  C3 = Electrolytic Capacitor [capacitance=1µF package="100 mil [THT, electrolytic]"]
  C4 = Electrolytic Capacitor [capacitance=1µF package="100 mil [THT, electrolytic]"]
  R10 = Resistor [tolerance=±5% resistance=100 package=THT]
  R11 = Resistor [tolerance=±5% resistance=1k package=THT]

nets:
  N1: R1.Pin_0, C1.-, R2.leg1, Q1.gate, R4.Pin_1, Q2.B, IC1.A_V-, C2.1, LED1.cathode, C3.-, C4.-, R11.Pin_0
  N2: C1.+, IC1.A_V+, C2.0
  N3: R2.leg2, R6.Pin_1, C4.+
  N4: D1.cathode, R3.leg1
  N5: R3.wiper, R7.wiper, R8.wiper, IC1.B_+IN, C3.+
  N6: Q1.drain, R4.Pin_0
  N7: Q1.source, R5.leg1
  N8: R5.wiper, Q2.C
  N9: R5.leg2, R6.Pin_0
  N10: Q2.E, R7.leg2
  N11: D2.anode, R8.leg1
  N12: IC1.A_OUT, IC1.A_-IN, R9.Pin_1
  N13: IC1.A_+IN, IC1.B_-IN, IC1.B_OUT, R10.Pin_1
  N14: R9.Pin_0, LED1.anode
  N15: R10.Pin_0, R11.Pin_1

notes:
  SyncIn
  GND
  +5V
  GND
  +9V
  Level
  10k/A
  Attack
  50k/A
  Sustain
  10k/A
  Decay
  50k/A
  Release
  50k/A
  OUT
  Indicator
