# Fritzing sketch Arduino_EG_r2 (saved by Fritzing 0.9.3b)
breadboards: 1

parts:
  パーツ1 = Arduino Pro Mini (5V)  # not connected
  R3 = Rotary Potentiometer (Small) [maximum_resistance=100kΩ package=THT]
  D1 = Rectifier Diode [part_number=1N4001 package="300 mil [THT]"]
  Q1 = Basic FET P-Channel [package="TO220 [THT]"]
  Q2 = PNP-Transistor [package="TO92 [THT]"]
  D2 = Rectifier Diode [part_number=1N4001 package="300 mil [THT]"]
  C1 = Electrolytic Capacitor [capacitance=1µF package="100 mil [THT, electrolytic]"]
  R5 = Resistor [tolerance=±5% resistance=1k package=THT]
  LED1 = LED - 5mm [color="Red (633nm)" package="5 mm [THT]"]
  IC1 = Dual Op-Amp [package=dip08]
  C2 = Ceramic Capacitor [capacitance=100nF package="100 mil [THT, multilayer]"]
  R6 = Resistor [tolerance=±5% resistance=2.2k package=THT]
  R7 = Resistor [tolerance=±5% resistance=4.7k package=THT]
  R8 = Resistor [tolerance=±5% resistance=4.7k package=THT]

nets:
  N1: R3.leg1, Q1.source
  N2: R3.wiper, Q2.C
  N3: R3.leg2, IC1.A_V+, C2.0
  N4: D1.cathode, R7.Pin_1
  N5: Q1.gate, Q2.B, C1.-, LED1.cathode, IC1.A_+IN, IC1.A_V-, C2.1
  N6: Q2.E, R8.Pin_1
  N7: D2.anode, R6.Pin_1
  N8: C1.+, IC1.B_+IN, R6.Pin_0, R7.Pin_0, R8.Pin_0
  N9: R5.Pin_0, LED1.anode
  N10: IC1.A_OUT, IC1.A_-IN
  N11: IC1.B_-IN, IC1.B_OUT

notes:
  Sustain
  10k/A
  OUT
  2N7000
  S / G / D
  2SA1015
  E / C / B
  GND
  +5V
  GateIn
  A
  R
  D
