# Fritzing sketch Arduino_EG_r3 (saved by Fritzing 0.9.3b)
breadboards: 1

parts:
  パーツ1 = Arduino Pro Mini (5V)  # not connected
  R3 = Rotary Potentiometer (Small) [maximum_resistance=100kΩ package=THT]
  D1 = Rectifier Diode [part_number=1N4001 package="300 mil [THT]"]
  Q1 = Basic FET P-Channel [package="TO220 [THT]"]
  Q2 = PNP-Transistor [package="TO92 [THT]"]
  D2 = Rectifier Diode [part_number=1N4001 package="300 mil [THT]"]
  C1 = Electrolytic Capacitor [capacitance=1µF package="100 mil [THT, electrolytic]"]
  R5 = Resistor [tolerance=±5% resistance=1k package=THT]
  IC1 = Dual Op-Amp [package=dip08]
  C2 = Ceramic Capacitor [capacitance=100nF package="100 mil [THT, multilayer]"]
  R9 = Resistor [tolerance=±5% resistance=6.8k package=THT]
  LED1 = LED - 3mm [color="Green (570nm)" package="3 mm [THT]"]
  R10 = Rotary Potentiometer (Small) [maximum_resistance=100kΩ package=THT]
  R11 = Rotary Potentiometer (Small) [maximum_resistance=100kΩ package=THT]
  R12 = Rotary Potentiometer (Small) [maximum_resistance=100kΩ package=THT]
  R13 = Resistor [tolerance=±5% resistance=1M package=THT]

nets:
  N1: R3.leg1, Q1.source
  N2: R3.wiper, Q2.C
  N3: R3.leg2, R9.Pin_0
  N4: D1.cathode, R11.wiper
  N5: Q1.gate, Q2.B, C1.-, IC1.A_V-, C2.1, LED1.cathode, R13.Pin_1
  N6: Q1.drain, R13.Pin_0
  N7: Q2.E, R12.leg1
  N8: D2.anode, R10.wiper
  N9: C1.+, IC1.B_+IN, R10.leg1, R11.leg1, R12.wiper
  N10: R5.Pin_0, IC1.A_OUT, IC1.A_-IN
  N11: R5.Pin_1, LED1.anode
  N12: IC1.A_+IN, IC1.B_-IN, IC1.B_OUT
  N13: IC1.A_V+, C2.0, R9.Pin_1

notes:
  Sustain
  10k/B
  OUT
  2N7000
  S / G / D
  2SA1015
  E / C / B
  GND
  +5V
  GateIn
  Attack
  10k/A
  Release
  10k/A
  Decay
  10k/A
