# Fritzing sketch Arduino_EG_ケース内配線 (saved by Fritzing 0.9.3b)
perfboards: 1

parts:
  J1 = female pin header, 2 pins [form="♀ (female)"]
  J2 = rounded female pin header, 2 pins [form="♀ (female rounded)"]
  J2_2 = female pin header, 3 pins [form="♀ (female)"]
  J3 = rounded female pin header, 2 pins [form="♀ (female rounded)"]
  J4 = rounded female pin header, 2 pins [form="♀ (female rounded)"]
  J5 = rounded female pin header, 2 pins [form="♀ (female rounded)"]
  Power_plug1 = Power plug
  S1 = Toggle Switch [package=THT]
  R1 = Rotary Potentiometer (Small) [maximum_resistance=100kΩ package=THT]
  J6 = rounded female pin header, 2 pins [form="♀ (female rounded)"]
  TRS1 = Audio Jack (TRS) 3.5mm [package="4Ucon 08780 [THT]"]
  TRS2 = Audio Jack (TRS) 3.5mm [package="4Ucon 08780 [THT]"]
  J7 = female pin header, 3 pins [form="♀ (female)"]
  R2 = Rotary Potentiometer (Small) [maximum_resistance=100kΩ package=THT]
  R3 = Rotary Potentiometer (Small) [maximum_resistance=100kΩ package=THT]
  R4 = Rotary Potentiometer (Small) [maximum_resistance=100kΩ package=THT]
  R5 = Rotary Potentiometer (Small) [maximum_resistance=100kΩ package=THT]
  J8 = female pin header, 2 pins [form="♀ (female)"]
  LED1 = LED - 5mm [color="Red (633nm)" package="5 mm [THT]"]

nets:
  N1: J1.pin1, S1.COM
  N2: J1.pin2, Power_plug1.GND
  N3: J2.pin1, TRS2.Tip
  N4: J2.pin2, TRS2.Sleeve
  N5: J2_2.pin1, R1.leg1
  N6: J2_2.pin2, R1.wiper
  N7: J2_2.pin3, R1.leg2
  N8: J3.pin1, TRS1.Tip
  N9: J3.pin2, TRS1.Sleeve
  N10: J4.pin1, R2.wiper, R2.leg2
  N11: J4.pin2, R2.leg1
  N12: J5.pin1, R3.wiper, R3.leg2
  N13: J5.pin2, R3.leg1
  N14: Power_plug1.VCC, S1.L1
  N15: J6.pin1, R4.leg1
  N16: J6.pin2, R4.wiper, R4.leg2
  N17: J7.pin1, R5.leg2
  N18: J7.pin2, R5.wiper
  N19: J7.pin3, R5.leg1
  N20: J8.pin1, LED1.cathode
  N21: J8.pin2, LED1.anode

notes:
  DC9V
  10k/A
  Level
  GateIn
  Out
  50k/A
  Attack
  50k/A
  Release
  50k/A
  Decay
  10k/A
  Sustain
